# Fritzing sketch Digitale_Sanduhr_03 (saved by Fritzing 1.0.1rc)
# 18650 Li-ion Battery: CC-BY Dr Kristofer Chan, King's College London/Remote-research.org
perfboards: 1

parts:
  LED_Matrix_02 = 8x8 LED Modul mit MAX7219 [package=THT]
  LED_Matrix_01 = 8x8 LED Modul mit MAX7219 [package=THT]
  D1_Mini = WeMos D1 Mini
  DHT-Sensor = DHT22 module
  TOUCH_01 = TTP223B Capacitive Touch Sensor Module
  Buzzer = Piezo Speaker
  Gyroskop-Sensor = MPU-6050 Board GY-521 [form="♀ (female)" package=THT]
  4in1_Lademodul = 2A 5V 4in1 Li-ion Battery Charger Discharge Module 3.7V 4.2V Charge Boost Board [chip_label="2A 5V 4in1 Li-ion Battery Charger Discharge Module"]
  Batteriehalter = battery_holder_single_18650
  Batterie = 18650 Li-ion Battery [package=battery-18650]
  TOUCH_02 = TTP223B Capacitive Touch Sensor Module
  RTC-Modul = Tiny RTC
  USB-C_Buchse = USB type C-05-power-only

nets:
  N1: LED_Matrix_02.VCC_Eingang, LED_Matrix_01.VCC_Ausgang
  N2: LED_Matrix_02.GND_Eingang, LED_Matrix_01.GND_Ausgang
  N3: LED_Matrix_02.DIN_Eingang, LED_Matrix_01.DOUT_Ausgang
  N4: LED_Matrix_02.CS_Eingang, LED_Matrix_01.CS_Ausgang
  N5: LED_Matrix_02.CLK_Eingang, LED_Matrix_01.CLK_Ausgang
  5V: LED_Matrix_01.VCC_Eingang, D1_Mini.5V, Gyroskop-Sensor.pin1, 4in1_Lademodul.Out-5V, RTC-Modul.VCC
  GND: LED_Matrix_01.GND_Eingang, D1_Mini.G, DHT-Sensor.-, TOUCH_01.GND, Buzzer.pin1, Gyroskop-Sensor.pin2, 4in1_Lademodul.GND#1, TOUCH_02.GND, RTC-Modul.GND
  N6: LED_Matrix_01.DIN_Eingang, D1_Mini.D8
  N7: LED_Matrix_01.CS_Eingang, D1_Mini.D3
  N8: LED_Matrix_01.CLK_Eingang, D1_Mini.D0
  VCC: D1_Mini.3V3, DHT-Sensor.+, TOUCH_01.VCC, Gyroskop-Sensor.pin7, TOUCH_02.VCC
  N9: D1_Mini.D1, RTC-Modul.SCL#7
  N10: D1_Mini.D2, RTC-Modul.SDA#8
  N11: D1_Mini.D4, DHT-Sensor.Out
  N12: D1_Mini.D5, TOUCH_01.SIG
  N13: D1_Mini.D6, TOUCH_02.SIG
  N14: D1_Mini.D7, Buzzer.pin2
  N15: Gyroskop-Sensor.pin3, RTC-Modul.SCL#1
  N16: Gyroskop-Sensor.pin4, RTC-Modul.SDA#2
  N17: 4in1_Lademodul.BAT, Batteriehalter.+#1, Batterie.+
  N18: 4in1_Lademodul.VIN, USB-C_Buchse.Pin_2
  N19: 4in1_Lademodul.GND#4, USB-C_Buchse.Pin_3
  N20: 4in1_Lademodul.GND#5, Batteriehalter.+#0, Batterie.-

custom parts:
  WeMos D1 Mini: The D1 mini is a mini wifi board based on ESP-8266EX.
  DHT22 module: DHT22 module. Pins VCC Data GND.
  TTP223B Capacitive Touch Sensor Module: The TTP223B capacitive touch sensor module uses the TTP223B IC. The appropriate voltage is approximately 2 to 5.5 volts.
  MPU-6050 Board GY-521: Acelerometro y Giroscopio MPU-6050 Board GY-521
  battery_holder_single_18650: single 18650 battery holder
  18650 Li-ion Battery: 18650 li-ion Battery Standard 18650 battery with interactive connectors Creative Common Attribution 4.0 International (CC-BY 4.0) license. Any use of this part requires attribution of Dr Kristofer Chan, Department of Geography, King's College London. Contact kristofer.chan [at] kcl.ac.uk OR kris [at] remote-research.org for further information.
  Tiny RTC: Tiny RTC I2C module DS1370Z RTC and AT24C32 EEPROM
